# Fritzing sketch BreadboardSketch (saved by Fritzing 0.9.2b)
circuit board: 8.46667cm x 5.64444cm
breadboards: 1

parts:
  Raspberry_Pi1 = Raspberry Pi 2
  S1 = Pushbutton [package="[THT]"]
  LED1 = LED - 5mm [color="Green (570nm)" package="5 mm [THT]"]
  LED2 = LED - 5mm [color="White (8000K)" package="5 mm [THT]"]
  LED3 = LED - 5mm [color="Red (633nm)" package="5 mm [THT]"]

nets:
  N1: Raspberry_Pi1.GPIO4, S1.Pin_3, S1.Pin_4
  N2: Raspberry_Pi1.GPIO17, LED1.anode
  N3: Raspberry_Pi1.GPIO27, LED2.anode
  N4: Raspberry_Pi1.GPIO22, LED3.anode
  N5: Raspberry_Pi1.GND, S1.Pin_1, S1.Pin_2, LED1.cathode, LED2.cathode, LED3.cathode
